# Fritzing sketch LaserReceiverTransistor (saved by Fritzing 0.8.5b)
breadboards: 1

parts:
  R2 = Resistor [tolerance=±5% resistance=10k package=THT]
  Q1 = Basic FET N-Channel [package="TO220 [THT]"]
  P2 = S1133 Si Photodiode [package="8mm Ceramic [THT]"]
  R1 = Resistor [tolerance=±5% resistance=200k package=THT]
  J1_(Rx) = female pin header, 1 pin [form="♀ (female)"]

nets:
  N1: R2.Pin_0, Q1.source, J1_(Rx).pin1
  GND: R2.Pin_1, R1.Pin_1
  N2: Q1.gate, P2.anode, R1.Pin_0
  3.3V: Q1.drain, P2.cathode
